// Logisim project 3BitSignedNum_Calculator.circ as structural Verilog: 3 circuits, main circuit main
// 3BitSignedNum_Calculator
module main (
  input  [1:0] Operation_Mode,
  input  A2,
  input  A1,
  input  A0,
  input  B2,
  input  B1,
  input  B0
);

  wire bcdto7_segment_1_a, bcdto7_segment_1_b, bcdto7_segment_1_c, bcdto7_segment_1_d, bcdto7_segment_1_e,
       bcdto7_segment_1_f, bcdto7_segment_1_g, calculator_1_c0, calculator_1_c1, calculator_1_c2,
       calculator_1_c3, calculator_1_c4, calculator_1_div_by_zero;

  Calculator calculator_1 (
    .A2(A2), .A1(A1), .A0(A0), .B2(B2), .B1(B1), .B0(B0), .Operation_Mode(Operation_Mode),
    .C4(calculator_1_c4), .C3(calculator_1_c3), .C2(calculator_1_c2), .C1(calculator_1_c1),
    .C0(calculator_1_c0), .Div_by_Zero(calculator_1_div_by_zero));
  BCDto7_Segment bcdto7_segment_1 (
    .C3(calculator_1_c3), .C2(calculator_1_c2), .C1(calculator_1_c1), .C0(calculator_1_c0),
    .Div_by_Zero(calculator_1_div_by_zero), .b(bcdto7_segment_1_b), .a(bcdto7_segment_1_a),
    .f(bcdto7_segment_1_f), .g(bcdto7_segment_1_g), .e(bcdto7_segment_1_e), .d(bcdto7_segment_1_d),
    .c(bcdto7_segment_1_c));
  _7_Segment_Display u_7_segment_display_1 (
    .g(bcdto7_segment_1_g), .f(bcdto7_segment_1_f), .a(bcdto7_segment_1_a), .b(bcdto7_segment_1_b),
    .e(bcdto7_segment_1_e), .d(bcdto7_segment_1_d), .c(bcdto7_segment_1_c));  // open: dp
  _7_Segment_Display u_7_segment_display_2 (.g(calculator_1_c4));  // open: f, a, b, e, d, c, dp
  LED Div_by_ZERO (.in(calculator_1_div_by_zero));
  // Simple_buzzer simple_buzzer_1: pin names not known; wires that end beside it: calculator_1_div_by_zero

  // Notes on the sheet:
  //   1
  //   4
  //   9
  //   15
  //   إبرام عاطف المصري سند
  //   أحمد إبراهيم حسن هاشم
  //   أحمد طه سيد محمد
  //   حمدي محمد سالم عبد التواب
  //   00: Add, 01: Subtract, 10: Multipluy, 11: Remainder
endmodule

// to7Segment
module BCDto7_Segment (
  input  C3,
  input  C2,
  input  C1,
  input  C0,
  input  Div_by_Zero,
  output b,
  output a,
  output f,
  output g,
  output e,
  output d,
  output c
);

  wire n7_segment_display_driver_1_p5, n7_segment_display_driver_1_p6, n7_segment_display_driver_1_p7,
       n7_segment_display_driver_1_p8, n7_segment_display_driver_1_p9, n7_segment_display_driver_1_p10,
       n7_segment_display_driver_1_p11, not_1_out;

  // _7_segment_display_driver 7_segment_display_driver_1: pin names not known; wires that end beside it: C3, C2, C1, C0, n7_segment_display_driver_1_p5, n7_segment_display_driver_1_p6, n7_segment_display_driver_1_p7, n7_segment_display_driver_1_p8, n7_segment_display_driver_1_p9, n7_segment_display_driver_1_p10, n7_segment_display_driver_1_p11
  not not_1 (not_1_out, Div_by_Zero);
  and and_1 (b, n7_segment_display_driver_1_p6, not_1_out);
  and and_2 (a, n7_segment_display_driver_1_p5, not_1_out);
  and and_3 (f, n7_segment_display_driver_1_p10, not_1_out);
  and and_4 (g, n7_segment_display_driver_1_p11, not_1_out);
  and and_5 (e, n7_segment_display_driver_1_p9, not_1_out);
  and and_6 (d, n7_segment_display_driver_1_p8, not_1_out);
  and and_7 (c, n7_segment_display_driver_1_p7, not_1_out);
endmodule

module Calculator (
  input  [1:0] Operation_Mode,
  input  A2,
  input  A1,
  input  A0,
  input  B2,
  input  B1,
  input  B0,
  output C4,
  output C3,
  output C2,
  output C1,
  output C0,
  output Div_by_Zero
);

  wire addersame_1_c0, addersame_1_c1, addersame_1_c2, addersame_1_c3, addersame_1_c4, main_1_c0, main_1_c1,
       main_1_c2, main_1_c3, main_1_c4, main_2_c0, main_2_c1, main_2_c2, main_2_c3, main_2_c4,
       main_2_div_by_zero, multiplexer_1_out, or_1_out, subtract_1_c0, subtract_1_c1, subtract_1_c2,
       subtract_1_c3, subtract_1_c4;

  AdderSame addersame_1 (
    .A2(A2), .A1(A1), .A0(A0), .B2(B2), .B1(B1), .B0(B0), .C4(addersame_1_c4), .C3(addersame_1_c3),
    .C2(addersame_1_c2), .C1(addersame_1_c1), .C0(addersame_1_c0));
  Subtract subtract_1 (
    .A2(A2), .A1(A1), .A0(A0), .B2(B2), .B1(B1), .B0(B0), .C4(subtract_1_c4), .C3(subtract_1_c3),
    .C2(subtract_1_c2), .C1(subtract_1_c1), .C0(subtract_1_c0));
  Multiplication_main main_1 (
    .A2(A2), .A1(A1), .A0(A0), .B2(B2), .B1(B1), .B0(B0), .C4(main_1_c4), .C3(main_1_c3), .C2(main_1_c2),
    .C1(main_1_c1), .C0(main_1_c0));
  Remainder_main main_2 (
    .A2(A2), .A1(A1), .A0(A0), .B2(B2), .B1(B1), .B0(B0), .C4(main_2_c4), .C3(main_2_c3), .C2(main_2_c2),
    .C1(main_2_c1), .C0(main_2_c0), .Div_by_ZERO(main_2_div_by_zero));
  Multiplexer #(.select(2)) multiplexer_1 (
    .in0(addersame_1_c4), .in1(subtract_1_c4), .in2(main_1_c4), .in3(main_2_c4), .out(multiplexer_1_out),
    .sel(Operation_Mode));  // open: en
  Multiplexer #(.select(2)) multiplexer_2 (
    .in0(addersame_1_c3), .in1(subtract_1_c3), .in2(main_1_c3), .in3(main_2_c3), .out(C3),
    .sel(Operation_Mode));  // open: en
  Multiplexer #(.select(2)) multiplexer_3 (
    .in0(addersame_1_c2), .in1(subtract_1_c2), .in2(main_1_c2), .in3(main_2_c2), .out(C2),
    .sel(Operation_Mode));  // open: en
  Multiplexer #(.select(2)) multiplexer_4 (
    .in0(addersame_1_c1), .in1(subtract_1_c1), .in2(main_1_c1), .in3(main_2_c1), .out(C1),
    .sel(Operation_Mode));  // open: en
  Multiplexer #(.select(2)) multiplexer_5 (
    .in0(addersame_1_c0), .in1(subtract_1_c0), .in2(main_1_c0), .in3(main_2_c0), .out(C0),
    .sel(Operation_Mode));  // open: en
  or or_1 (or_1_out, C0, C1, C2, C3);
  and and_1 (Div_by_Zero, Operation_Mode[0], Operation_Mode[1], main_2_div_by_zero);
  and and_2 (C4, multiplexer_1_out, or_1_out);
endmodule
