// Logisim project Add_Subtract.circ as structural Verilog
module main (
  input  A0,
  input  A1,
  input  A2,
  input  B0,
  input  B1,
  input  B2,
  output C0,
  output C1,
  output C2
);

  Full_Adder full_adder_1 (.A0(A0), .A1(A1), .A2(A2), .B0(B0), .B1(B1), .B2(B2), .S0(C0), .S1(C1), .S2(C2));
endmodule

module HalfAdder (
  input  bit_1,
  input  bit_2,
  output sum,
  output remainder
);

  xor xor_1 (sum, bit_1, bit_2);
  and and_1 (remainder, bit_2, bit_1);
endmodule

// Full_Adder
module Full_Adder (
  input  A0,
  input  A1,
  input  A2,
  input  B0,
  input  B1,
  input  B2,
  output S0,
  output S1,
  output S2
);

  wire halfadder_1_remainder, halfadder_2_remainder, halfadder_2_sum, halfadder_3_remainder;

  HalfAdder halfadder_1 (.bit_1(A0), .bit_2(B0), .sum(S0), .remainder(halfadder_1_remainder));
  HalfAdder halfadder_2 (
    .bit_1(halfadder_1_remainder), .bit_2(A1), .sum(halfadder_2_sum), .remainder(halfadder_2_remainder));
  HalfAdder halfadder_3 (.bit_1(halfadder_2_sum), .bit_2(B1), .sum(S1), .remainder(halfadder_3_remainder));
  HalfAdder halfadder_4 (.bit_1(halfadder_2_remainder), .bit_2(halfadder_3_remainder), .sum(S2));  // open: remainder
endmodule

module complement (
  input  a2,
  input  a1,
  input  a0,
  output out_4,
  output out_5,
  output out_6
);

  wire and_1_out, and_2_out, not_1_out, not_2_out, not_3_out, or_1_out;

  not not_1 (not_1_out, a0);
  not not_2 (not_2_out, a2);
  not not_3 (not_3_out, a1);
  or or_1 (or_1_out, a1, a0);
  and and_1 (and_1_out, not_2_out, or_1_out);
  and and_2 (and_2_out, a2, not_3_out, not_1_out);
  xor xor_1 (out_5, a1, a0);
  or or_2 (out_4, and_1_out, and_2_out);

  assign out_6 = a0;
endmodule

// Add
module AdderSame (
  input  A2,
  input  A1,
  input  A0,
  input  B2,
  input  B1,
  input  B0,
  output C4,
  output C3,
  output C2,
  output C1,
  output C0
);

  wire full_adder_1_s0, full_adder_1_s1, full_adder_1_s2, subtractor_1_out_7, subtractor_1_out_8,
       subtractor_1_out_9, xor_1_out;

  Full_Adder full_adder_1 (
    .A0(A0), .A1(A1), .A2(A2), .B0(B0), .B1(B1), .B2(B2), .S0(full_adder_1_s0), .S1(full_adder_1_s1),
    .S2(full_adder_1_s2));
  Subtractor subtractor_1 (
    .in_1(A0), .in_2(A1), .in_3(A2), .in_4(B0), .in_5(B1), .in_6(B2), .out_7(subtractor_1_out_7),
    .out_8(subtractor_1_out_8), .out_9(subtractor_1_out_9));
  xor xor_1 (xor_1_out, A2, B2);
  Multiplexer multiplexer_1 (.in0(full_adder_1_s0), .in1(subtractor_1_out_7), .out(C0), .sel(xor_1_out));  // open: en
  Multiplexer multiplexer_2 (.in0(full_adder_1_s1), .in1(subtractor_1_out_8), .out(C1), .sel(xor_1_out));  // open: en
  Multiplexer multiplexer_3 (.in0(full_adder_1_s2), .in1(1'b0), .out(C2), .sel(xor_1_out));  // open: en
  Multiplexer multiplexer_4 (.in0(1'b0), .in1(1'b0), .out(C3), .sel(xor_1_out));  // open: en
  Multiplexer multiplexer_5 (.in0(A2), .in1(subtractor_1_out_9), .out(C4), .sel(xor_1_out));  // open: en
endmodule

module Comparator (
  input  A0,
  input  A1,
  input  B0,
  input  B1,
  output out_5,
  output out_6
);

  wire and_1_out, and_2_out, and_3_out, and_4_out, and_5_out, and_6_out, not_1_out, not_2_out, not_3_out,
       not_4_out, not_5_out, or_1_out;

  not not_1 (not_1_out, B1);
  not not_2 (not_2_out, B0);
  and and_1 (and_1_out, A1, not_1_out);
  not not_3 (not_3_out, A1);
  and and_2 (and_2_out, A0, not_2_out);
  not not_4 (not_4_out, A0);
  and and_3 (and_3_out, not_3_out, B1);
  and and_4 (and_4_out, not_4_out, B0);
  or or_1 (or_1_out, and_1_out, and_3_out);
  not not_5 (not_5_out, or_1_out);
  and and_5 (and_5_out, not_5_out, and_2_out);
  and and_6 (and_6_out, not_5_out, and_4_out);
  or or_2 (out_5, and_1_out, and_5_out);
  or or_3 (out_6, and_6_out, and_3_out);
endmodule

module GetMin (
  input  A0,
  input  A1,
  input  A2,
  input  B0,
  input  B1,
  input  B2,
  output out_7,
  output out_8,
  output out_9
);

  wire and_1_out, and_2_out, and_3_out, and_4_out, and_5_out, and_6_out, not_1_out, not_2_out, not_3_out,
       not_4_out, not_5_out, or_1_out, or_2_out;

  not not_1 (not_1_out, B1);
  not not_2 (not_2_out, B0);
  and and_1 (and_1_out, A1, not_1_out);
  not not_3 (not_3_out, A1);
  and and_2 (and_2_out, A0, not_2_out);
  not not_4 (not_4_out, A0);
  and and_3 (and_3_out, not_3_out, B1);
  and and_4 (and_4_out, not_4_out, B0);
  or or_1 (or_1_out, and_1_out, and_3_out);
  not not_5 (not_5_out, or_1_out);
  and and_5 (and_5_out, not_5_out, and_2_out);
  and and_6 (and_6_out, not_5_out, and_4_out);
  or or_2 (or_2_out, and_1_out, and_5_out);
  // OR_Gate or_3 has open pins: in0=and_6_out, in1=and_3_out, out=open
  Multiplexer multiplexer_1 (.in0(A0), .in1(B0), .out(out_7), .sel(or_2_out));  // open: en
  Multiplexer multiplexer_2 (.in0(A1), .in1(B1), .out(out_8), .sel(or_2_out));  // open: en
  Multiplexer multiplexer_3 (.in0(A2), .in1(B2), .out(out_9), .sel(or_2_out));  // open: en

  // Notes on the sheet:
  //   It's repalced by getMinMax citrcuit
endmodule

module GetMax (
  input  A0,
  input  A1,
  input  A2,
  input  B0,
  input  B1,
  input  B2,
  output out_7,
  output out_8,
  output out_9
);

  wire and_1_out, and_2_out, and_3_out, and_4_out, and_5_out, and_6_out, not_1_out, not_2_out, not_3_out,
       not_4_out, not_5_out, or_1_out, or_3_out;

  not not_1 (not_1_out, B1);
  not not_2 (not_2_out, B0);
  and and_1 (and_1_out, A1, not_1_out);
  not not_3 (not_3_out, A1);
  and and_2 (and_2_out, A0, not_2_out);
  not not_4 (not_4_out, A0);
  and and_3 (and_3_out, not_3_out, B1);
  and and_4 (and_4_out, not_4_out, B0);
  or or_1 (or_1_out, and_1_out, and_3_out);
  not not_5 (not_5_out, or_1_out);
  and and_5 (and_5_out, not_5_out, and_2_out);
  and and_6 (and_6_out, not_5_out, and_4_out);
  // OR_Gate or_2 has open pins: in0=and_1_out, in1=and_5_out, out=open
  or or_3 (or_3_out, and_6_out, and_3_out);
  Multiplexer multiplexer_1 (.in0(A0), .in1(B0), .out(out_7), .sel(or_3_out));  // open: en
  Multiplexer multiplexer_2 (.in0(A1), .in1(B1), .out(out_8), .sel(or_3_out));  // open: en
  Multiplexer multiplexer_3 (.in0(A2), .in1(B2), .out(out_9), .sel(or_3_out));  // open: en

  // Notes on the sheet:
  //   It's repalced by getMinMax citrcuit
endmodule

module Subtractor (
  input  in_1,
  input  in_2,
  input  in_3,
  input  in_4,
  input  in_5,
  input  in_6,
  output out_7,
  output out_8,
  output out_9
);

  wire complement_1_out_5, complement_1_out_6, getminmax_1_maxcenter, getminmax_1_maxup,
       getminmax_1_mincenter, getminmax_1_minup;

  getMinMax getminmax_1 (
    .A0(in_1), .A1(in_2), .A2(in_3), .B0(in_4), .B1(in_5), .B2(in_6), .maxup(getminmax_1_maxup),
    .maxcenter(getminmax_1_maxcenter), .maxdown(out_9), .minup(getminmax_1_minup),
    .mincenter(getminmax_1_mincenter));  // open: mindown
  complement complement_1 (
    .a1(getminmax_1_mincenter), .a0(getminmax_1_minup), .out_5(complement_1_out_5), .out_6(complement_1_out_6));  // open: a2, out_4
  Full_Adder full_adder_1 (
    .A0(getminmax_1_maxup), .A1(getminmax_1_maxcenter), .B0(complement_1_out_6), .B1(complement_1_out_5),
    .S0(out_7), .S1(out_8));  // open: A2, B2, S2
endmodule

module Subtract (
  input  A2,
  input  A1,
  input  A0,
  input  B2,
  input  B1,
  input  B0,
  output C4,
  output C3,
  output C2,
  output C1,
  output C0
);

  wire not_1_out;

  not not_1 (not_1_out, B2);
  AdderSame addersame_1 (
    .A2(A2), .A1(A1), .A0(A0), .B2(not_1_out), .B1(B1), .B0(B0), .C4(C4), .C3(C3), .C2(C2), .C1(C1), .C0(C0));
endmodule

module getMinMax (
  input  A0,
  input  A1,
  input  A2,
  input  B0,
  input  B1,
  input  B2,
  output maxup,
  output maxcenter,
  output maxdown,
  output minup,
  output mincenter,
  output mindown
);

  wire and_1_out, and_2_out, and_3_out, and_4_out, and_5_out, and_6_out, not_1_out, not_2_out, not_3_out,
       not_4_out, not_5_out, or_1_out, or_2_out, or_3_out;

  not not_1 (not_1_out, B1);
  not not_2 (not_2_out, B0);
  and and_1 (and_1_out, A1, not_1_out);
  not not_3 (not_3_out, A1);
  and and_2 (and_2_out, A0, not_2_out);
  not not_4 (not_4_out, A0);
  and and_3 (and_3_out, not_3_out, B1);
  and and_4 (and_4_out, not_4_out, B0);
  or or_1 (or_1_out, and_1_out, and_3_out);
  not not_5 (not_5_out, or_1_out);
  and and_5 (and_5_out, not_5_out, and_2_out);
  and and_6 (and_6_out, not_5_out, and_4_out);
  or or_2 (or_2_out, and_1_out, and_5_out);
  or or_3 (or_3_out, and_6_out, and_3_out);
  Multiplexer multiplexer_1 (.in0(A0), .in1(B0), .out(maxup), .sel(or_3_out));  // open: en
  Multiplexer multiplexer_2 (.in0(A1), .in1(B1), .out(maxcenter), .sel(or_3_out));  // open: en
  Multiplexer multiplexer_3 (.in0(A2), .in1(B2), .out(maxdown), .sel(or_3_out));  // open: en
  Multiplexer multiplexer_4 (.in0(A0), .in1(B0), .out(minup), .sel(or_2_out));  // open: en
  Multiplexer multiplexer_5 (.in0(A1), .in1(B1), .out(mincenter), .sel(or_2_out));  // open: en
  Multiplexer multiplexer_6 (.in0(A2), .in1(B2), .out(mindown), .sel(or_2_out));  // open: en
endmodule

module test (
  input  A0,
  input  A1,
  input  A2,
  input  B0,
  input  B1,
  input  B2,
  output maxup,
  output maxcenter,
  output maxdown,
  output minup,
  output mincenter,
  output mindown
);

  wire and_1_out, and_2_out, and_3_out, and_4_out, not_1_out, not_2_out, not_3_out, not_4_out, not_5_out,
       or_1_out, or_2_out;

  not not_1 (not_1_out, B1);
  not not_2 (not_2_out, B0);
  and and_1 (and_1_out, A1, not_1_out);
  not not_3 (not_3_out, A1);
  and and_2 (and_2_out, A0, not_2_out);
  and and_3 (and_3_out, not_3_out, B1);
  or or_1 (or_1_out, and_1_out, and_3_out);
  not not_4 (not_4_out, or_1_out);
  and and_4 (and_4_out, not_4_out, and_2_out);
  or or_2 (or_2_out, and_1_out, and_4_out);
  not not_5 (not_5_out, or_2_out);
  Multiplexer multiplexer_1 (.in0(A0), .in1(B0), .out(maxup), .sel(not_5_out));  // open: en
  Multiplexer multiplexer_2 (.in0(A1), .in1(B1), .out(maxcenter), .sel(not_5_out));  // open: en
  Multiplexer multiplexer_3 (.in0(A2), .in1(B2), .out(maxdown), .sel(not_5_out));  // open: en
  Multiplexer multiplexer_4 (.in0(A0), .in1(B0), .out(minup), .sel(or_2_out));  // open: en
  Multiplexer multiplexer_5 (.in0(A1), .in1(B1), .out(mincenter), .sel(or_2_out));  // open: en
  Multiplexer multiplexer_6 (.in0(A2), .in1(B2), .out(mindown), .sel(or_2_out));  // open: en
endmodule
