// Logisim project Remainder.circ as structural Verilog: 2 circuits, main circuit main
// Remainder
module main (
  input  A2,
  input  A1,
  input  A0,
  input  B2,
  input  B1,
  input  B0,
  output C4,
  output C3,
  output C2,
  output C1,
  output C0,
  output Div_by_ZERO
);

  wire and_1_out, and_2_out, and_3_out, nand_1_out, not_1_out;

  not not_1 (not_1_out, A0);
  and and_1 (and_1_out, A1, not_1_out);
  and and_2 (and_2_out, B1, B0);
  and and_3 (and_3_out, A0, B1);
  and and_4 (C0, and_3_out, nand_1_out);
  nand nand_1 (nand_1_out, A1, B0);
  and and_5 (C1, and_1_out, and_2_out);
  nor nor_1 (Div_by_ZERO, B0, B1);

  assign C2 = 1'b0;
  assign C3 = 1'b0;
  assign C4 = A2;
endmodule

// Mod_Calc
module _3BitSignedNum_Mod (
  input  A2,
  input  A1,
  input  A0,
  input  B2,
  input  B1,
  input  B0,
  output C4,
  output C1,
  output C0,
  output Div_by_ZERO
);

  wire and_1_out, and_2_out, and_3_out, and_6_out, and_7_out, and_8_out, and_9_out, and_10_out, and_11_out,
       n7_segment_display_driver_1_p5, n7_segment_display_driver_1_p6, n7_segment_display_driver_1_p7,
       n7_segment_display_driver_1_p8, n7_segment_display_driver_1_p9, n7_segment_display_driver_1_p10,
       n7_segment_display_driver_1_p11, nand_1_out, not_1_out, not_2_out;

  not not_1 (not_1_out, A0);
  and and_1 (and_1_out, A1, not_1_out);
  and and_2 (and_2_out, B1, B0);
  and and_3 (and_3_out, A0, B1);
  and and_4 (C0, and_3_out, nand_1_out);
  nand nand_1 (nand_1_out, A1, B0);
  and and_5 (C1, and_1_out, and_2_out);
  nor nor_1 (Div_by_ZERO, B0, B1);
  // _7_segment_display_driver 7_segment_display_driver_1: pin names not known; wires that end beside it: 1'b0, 1'b0, C1, C0, n7_segment_display_driver_1_p5, n7_segment_display_driver_1_p6, n7_segment_display_driver_1_p7, n7_segment_display_driver_1_p8, n7_segment_display_driver_1_p9, n7_segment_display_driver_1_p10, n7_segment_display_driver_1_p11
  not not_2 (not_2_out, Div_by_ZERO);
  LED Negative_Sign (.in(A2));
  LED u_Div_by_Zero (.in(Div_by_ZERO));
  // Simple_buzzer simple_buzzer_1: pin names not known; wires that end beside it: Div_by_ZERO
  and and_6 (and_6_out, n7_segment_display_driver_1_p6, not_2_out);
  and and_7 (and_7_out, n7_segment_display_driver_1_p5, not_2_out);
  and and_8 (and_8_out, n7_segment_display_driver_1_p10, not_2_out);
  and and_9 (and_9_out, n7_segment_display_driver_1_p9, not_2_out);
  and and_10 (and_10_out, n7_segment_display_driver_1_p8, not_2_out);
  and and_11 (and_11_out, n7_segment_display_driver_1_p7, not_2_out);
  _7_Segment_Display u_7_segment_display_1 (
    .g(n7_segment_display_driver_1_p11), .f(and_8_out), .a(and_7_out), .b(and_6_out), .e(and_9_out),
    .d(and_10_out), .c(and_11_out));  // open: dp

  assign C4 = A2;
endmodule
